// Logisim project step2.circ as structural Verilog: 15 circuits, main circuit Register File
// REGFILE
module Register_File (
  input  [3:0] SRC1,
  input  [3:0] SRC2,
  input  [15:0] InData,
  input  [3:0] DST,
  input  WE,
  input  Clock,
  output [15:0] OutData2,
  output [15:0] OutData1
);

  wire and_1_out, and_2_out, and_3_out, and_4_out, and_5_out, and_6_out, and_7_out, and_8_out, and_9_out,
       and_10_out, and_11_out, and_12_out, and_13_out, and_14_out, and_15_out, and_16_out, decoder_1_out0,
       decoder_1_out1, decoder_1_out2, decoder_1_out3, decoder_1_out4, decoder_1_out5, decoder_1_out6,
       decoder_1_out7, decoder_1_out8, decoder_1_out9, decoder_1_out10, decoder_1_out11, decoder_1_out12,
       decoder_1_out13, decoder_1_out14, decoder_1_out15, decoder_2_out0, decoder_2_out1, decoder_2_out2,
       decoder_2_out3, decoder_2_out4, decoder_2_out5, decoder_2_out6, decoder_2_out7, decoder_2_out8,
       decoder_2_out9, decoder_2_out10, decoder_2_out11, decoder_2_out12, decoder_2_out13, decoder_2_out14,
       decoder_2_out15, decoder_3_out0, decoder_3_out1, decoder_3_out2, decoder_3_out3, decoder_3_out4,
       decoder_3_out5, decoder_3_out6, decoder_3_out7, decoder_3_out8, decoder_3_out9, decoder_3_out10,
       decoder_3_out11, decoder_3_out12, decoder_3_out13, decoder_3_out14, decoder_3_out15;
  wire [15:0] R00_q, R01_q, R02_q, R03_q, R04_q, R05_q, R06_q, R07_q, R08_q, R09_q, R10_q, R11_q, R12_q,
       R13_q, R14_q, R15_q;

  Decoder #(.select(4), .enable("false")) decoder_1 (
    .out0(decoder_1_out0), .out1(decoder_1_out1), .out2(decoder_1_out2), .out3(decoder_1_out3),
    .out4(decoder_1_out4), .out5(decoder_1_out5), .out6(decoder_1_out6), .out7(decoder_1_out7),
    .out8(decoder_1_out8), .out9(decoder_1_out9), .out10(decoder_1_out10), .out11(decoder_1_out11),
    .out12(decoder_1_out12), .out13(decoder_1_out13), .out14(decoder_1_out14), .out15(decoder_1_out15),
    .sel(DST));
  Decoder #(.select(4), .enable("false")) decoder_2 (
    .out0(decoder_2_out0), .out1(decoder_2_out1), .out2(decoder_2_out2), .out3(decoder_2_out3),
    .out4(decoder_2_out4), .out5(decoder_2_out5), .out6(decoder_2_out6), .out7(decoder_2_out7),
    .out8(decoder_2_out8), .out9(decoder_2_out9), .out10(decoder_2_out10), .out11(decoder_2_out11),
    .out12(decoder_2_out12), .out13(decoder_2_out13), .out14(decoder_2_out14), .out15(decoder_2_out15),
    .sel(SRC1));
  Decoder #(.select(4), .enable("false")) decoder_3 (
    .out0(decoder_3_out0), .out1(decoder_3_out1), .out2(decoder_3_out2), .out3(decoder_3_out3),
    .out4(decoder_3_out4), .out5(decoder_3_out5), .out6(decoder_3_out6), .out7(decoder_3_out7),
    .out8(decoder_3_out8), .out9(decoder_3_out9), .out10(decoder_3_out10), .out11(decoder_3_out11),
    .out12(decoder_3_out12), .out13(decoder_3_out13), .out14(decoder_3_out14), .out15(decoder_3_out15),
    .sel(SRC2));
  and and_1 (and_1_out, decoder_1_out0, WE);
  and and_2 (and_2_out, decoder_1_out1, WE);
  and and_3 (and_3_out, decoder_1_out2, WE);
  and and_4 (and_4_out, decoder_1_out3, WE);
  and and_5 (and_5_out, decoder_1_out4, WE);
  and and_6 (and_6_out, decoder_1_out5, WE);
  and and_7 (and_7_out, decoder_1_out6, WE);
  and and_8 (and_8_out, decoder_1_out7, WE);
  and and_9 (and_9_out, decoder_1_out8, WE);
  and and_10 (and_10_out, decoder_1_out9, WE);
  and and_11 (and_11_out, decoder_1_out10, WE);
  and and_12 (and_12_out, decoder_1_out11, WE);
  and and_13 (and_13_out, decoder_1_out12, WE);
  and and_14 (and_14_out, decoder_1_out13, WE);
  and and_15 (and_15_out, decoder_1_out14, WE);
  and and_16 (and_16_out, decoder_1_out15, WE);
  Register #(.width(16)) R00 (.D(InData), .en(and_1_out), .Q(R00_q), .clk(Clock), .clr(1'b0));
  Register #(.width(16)) R01 (.D(InData), .en(and_2_out), .Q(R01_q), .clk(Clock), .clr(1'b0));
  Register #(.width(16)) R02 (.D(InData), .en(and_3_out), .Q(R02_q), .clk(Clock), .clr(1'b0));
  Register #(.width(16)) R03 (.D(InData), .en(and_4_out), .Q(R03_q), .clk(Clock), .clr(1'b0));
  Register #(.width(16)) R04 (.D(InData), .en(and_5_out), .Q(R04_q), .clk(Clock), .clr(1'b0));
  Register #(.width(16)) R05 (.D(InData), .en(and_6_out), .Q(R05_q), .clk(Clock), .clr(1'b0));
  Register #(.width(16)) R06 (.D(InData), .en(and_7_out), .Q(R06_q), .clk(Clock), .clr(1'b0));
  Register #(.width(16)) R07 (.D(InData), .en(and_8_out), .Q(R07_q), .clk(Clock), .clr(1'b0));
  Register #(.width(16)) R08 (.D(InData), .en(and_9_out), .Q(R08_q), .clk(Clock), .clr(1'b0));
  Register #(.width(16)) R09 (.D(InData), .en(and_10_out), .Q(R09_q), .clk(Clock), .clr(1'b0));
  Register #(.width(16)) R10 (.D(InData), .en(and_11_out), .Q(R10_q), .clk(Clock), .clr(1'b0));
  Register #(.width(16)) R11 (.D(InData), .en(and_12_out), .Q(R11_q), .clk(Clock), .clr(1'b0));
  Register #(.width(16)) R12 (.D(InData), .en(and_13_out), .Q(R12_q), .clk(Clock), .clr(1'b0));
  Register #(.width(16)) R13 (.D(InData), .en(and_14_out), .Q(R13_q), .clk(Clock), .clr(1'b0));
  Register #(.width(16)) R14 (.D(InData), .en(and_15_out), .Q(R14_q), .clk(Clock), .clr(1'b0));
  Register #(.width(16)) R15 (.D(InData), .en(and_16_out), .Q(R15_q), .clk(Clock), .clr(1'b0));
  assign OutData1 = decoder_2_out12 ? R12_q : 16'bz;  // Controlled_Buffer controlled_buffer_1
  assign OutData1 = decoder_2_out13 ? R13_q : 16'bz;  // Controlled_Buffer controlled_buffer_2
  assign OutData1 = decoder_2_out14 ? R14_q : 16'bz;  // Controlled_Buffer controlled_buffer_3
  assign OutData1 = decoder_2_out15 ? R15_q : 16'bz;  // Controlled_Buffer controlled_buffer_4
  assign OutData1 = decoder_2_out4 ? R04_q : 16'bz;  // Controlled_Buffer controlled_buffer_5
  assign OutData1 = decoder_2_out5 ? R05_q : 16'bz;  // Controlled_Buffer controlled_buffer_6
  assign OutData1 = decoder_2_out6 ? R06_q : 16'bz;  // Controlled_Buffer controlled_buffer_7
  assign OutData1 = decoder_2_out7 ? R07_q : 16'bz;  // Controlled_Buffer controlled_buffer_8
  assign OutData1 = decoder_2_out8 ? R08_q : 16'bz;  // Controlled_Buffer controlled_buffer_9
  assign OutData1 = decoder_2_out9 ? R09_q : 16'bz;  // Controlled_Buffer controlled_buffer_10
  assign OutData1 = decoder_2_out10 ? R10_q : 16'bz;  // Controlled_Buffer controlled_buffer_11
  assign OutData1 = decoder_2_out11 ? R11_q : 16'bz;  // Controlled_Buffer controlled_buffer_12
  assign OutData1 = decoder_2_out0 ? R00_q : 16'bz;  // Controlled_Buffer controlled_buffer_13
  assign OutData1 = decoder_2_out1 ? R01_q : 16'bz;  // Controlled_Buffer controlled_buffer_14
  assign OutData1 = decoder_2_out2 ? R02_q : 16'bz;  // Controlled_Buffer controlled_buffer_15
  assign OutData1 = decoder_2_out3 ? R03_q : 16'bz;  // Controlled_Buffer controlled_buffer_16
  assign OutData2 = decoder_3_out15 ? R15_q : 16'bz;  // Controlled_Buffer controlled_buffer_17
  assign OutData2 = decoder_3_out7 ? R07_q : 16'bz;  // Controlled_Buffer controlled_buffer_18
  assign OutData2 = decoder_3_out8 ? R08_q : 16'bz;  // Controlled_Buffer controlled_buffer_19
  assign OutData2 = decoder_3_out9 ? R09_q : 16'bz;  // Controlled_Buffer controlled_buffer_20
  assign OutData2 = decoder_3_out10 ? R10_q : 16'bz;  // Controlled_Buffer controlled_buffer_21
  assign OutData2 = decoder_3_out11 ? R11_q : 16'bz;  // Controlled_Buffer controlled_buffer_22
  assign OutData2 = decoder_3_out12 ? R12_q : 16'bz;  // Controlled_Buffer controlled_buffer_23
  assign OutData2 = decoder_3_out13 ? R13_q : 16'bz;  // Controlled_Buffer controlled_buffer_24
  assign OutData2 = decoder_3_out14 ? R14_q : 16'bz;  // Controlled_Buffer controlled_buffer_25
  assign OutData2 = decoder_3_out0 ? R00_q : 16'bz;  // Controlled_Buffer controlled_buffer_26
  assign OutData2 = decoder_3_out1 ? R01_q : 16'bz;  // Controlled_Buffer controlled_buffer_27
  assign OutData2 = decoder_3_out2 ? R02_q : 16'bz;  // Controlled_Buffer controlled_buffer_28
  assign OutData2 = decoder_3_out3 ? R03_q : 16'bz;  // Controlled_Buffer controlled_buffer_29
  assign OutData2 = decoder_3_out4 ? R04_q : 16'bz;  // Controlled_Buffer controlled_buffer_30
  assign OutData2 = decoder_3_out5 ? R05_q : 16'bz;  // Controlled_Buffer controlled_buffer_31
  assign OutData2 = decoder_3_out6 ? R06_q : 16'bz;  // Controlled_Buffer controlled_buffer_32
endmodule

// SPLITTER
module Splitter (
  input  [17:0] InstructionData,
  output [3:0] AL_LD_DST,
  output [14:0] Jump_ADDR,
  output [3:0] ST_SRC,
  output [2:0] Opcode,
  output [3:0] AL_SRC1,
  output [3:0] AL_SRC2,
  output Imm_Decider_bit,
  output [2:0] nzp,
  output [5:0] ImmData,
  output [3:0] OP1,
  output [3:0] OP2,
  output [3:0] BR_ADDR,
  output [10:0] LD_ST_ADDR
);


  assign AL_LD_DST = InstructionData[14:11];
  assign AL_SRC1 = InstructionData[10:7];
  assign AL_SRC2 = InstructionData[5:2];
  assign BR_ADDR = InstructionData[3:0];
  assign Imm_Decider_bit = InstructionData[6];
  assign ImmData = InstructionData[5:0];
  assign Jump_ADDR = InstructionData[14:0];
  assign LD_ST_ADDR = InstructionData[10:0];
  assign nzp = InstructionData[14:12];
  assign OP1 = InstructionData[11:8];
  assign OP2 = InstructionData[7:4];
  assign Opcode = InstructionData[17:15];
  assign ST_SRC = InstructionData[14:11];
endmodule

// ALU
module Main (
  output carry_out
);

  wire BRANCH_result_t_f, clock_1_out, control_unit_1_aluenable, control_unit_1_br_en,
       control_unit_1_datamemread, control_unit_1_datamemwrite, control_unit_1_pc_1, control_unit_1_pcwrite,
       control_unit_1_regwrite, not_1_out, not_2_out, splitter_1_imm_decider_bit;
  wire [1:0] control_unit_1_alucontrol;
  wire [2:0] control_unit_1_brcontrol, splitter_1_nzp, splitter_1_opcode;
  wire [3:0] multiplexer_2_out, multiplexer_3_out, multiplexer_4_out, splitter_1_al_ld_dst,
       splitter_1_al_src1, splitter_1_al_src2, splitter_1_br_addr, splitter_1_op1, splitter_1_op2,
       splitter_1_st_src;
  wire [5:0] splitter_1_immdata;
  wire [10:0] splitter_1_ld_st_addr;
  wire [14:0] _4to15zExtend_out_2, _11to15zExtend_out_2, multiplexer_1_out, pc_1_outputaddress,
       splitter_1_jump_addr;
  wire [15:0] _6to16sExtend__16bitouput, alu_16bit_1_alu_out, multiplexer_5_out, multiplexer_6_out,
       ram_1_data, register_file_1_outdata1, register_file_1_outdata2;
  wire [17:0] rom_1_data;

  Multiplexer #(.width(15), .enable("false")) multiplexer_1 (
    .in0(splitter_1_jump_addr), .in1(_4to15zExtend_out_2), .out(multiplexer_1_out), .sel(BRANCH_result_t_f));
  Clock clock_1 (.out(clock_1_out));
  PC pc_1 (
    .InputAddress(multiplexer_1_out), .PCWrite(control_unit_1_pcwrite), .PC_1(control_unit_1_pc_1),
    .Clock(clock_1_out), .OutputAddress(pc_1_outputaddress));
  _4to15zExtend _4to15zExtend (.in_1(splitter_1_br_addr), .out_2(_4to15zExtend_out_2));
  ROM #(.addrWidth(15), .dataWidth(18)) rom_1 (.addr(pc_1_outputaddress), .data(rom_1_data));  // open: sel
  Control_Unit control_unit_1 (
    .Opcode(splitter_1_opcode), .nzp(splitter_1_nzp), .Clock(clock_1_out),
    .ALUEnable(control_unit_1_aluenable), .ALUControl(control_unit_1_alucontrol), .PC_1(control_unit_1_pc_1),
    .DataMemRead(control_unit_1_datamemread), .RegWrite(control_unit_1_regwrite),
    .DataMemWrite(control_unit_1_datamemwrite), .PCWrite(control_unit_1_pcwrite),
    .BR_en(control_unit_1_br_en), .BRControl(control_unit_1_brcontrol));
  Splitter splitter_1 (
    .InstructionData(rom_1_data), .Opcode(splitter_1_opcode), .nzp(splitter_1_nzp),
    .Imm_Decider_bit(splitter_1_imm_decider_bit), .AL_LD_DST(splitter_1_al_ld_dst),
    .Jump_ADDR(splitter_1_jump_addr), .ST_SRC(splitter_1_st_src), .AL_SRC1(splitter_1_al_src1),
    .AL_SRC2(splitter_1_al_src2), .ImmData(splitter_1_immdata), .OP1(splitter_1_op1), .OP2(splitter_1_op2),
    .BR_ADDR(splitter_1_br_addr), .LD_ST_ADDR(splitter_1_ld_st_addr));
  not not_1 (not_1_out, splitter_1_imm_decider_bit);
  Multiplexer #(.width(4), .enable("false")) multiplexer_2 (
    .in0(splitter_1_al_src2), .in1(splitter_1_op2), .out(multiplexer_2_out), .sel(control_unit_1_br_en));
  Branch__Signed_Comparator_16bit BRANCH (
    .result_T_F(BRANCH_result_t_f), .Branch_Control(control_unit_1_brcontrol), .B(register_file_1_outdata2),
    .A(register_file_1_outdata1), .BR_en(control_unit_1_br_en));
  not not_2 (not_2_out, control_unit_1_datamemwrite);
  Multiplexer #(.width(4), .enable("false")) multiplexer_3 (
    .in0(splitter_1_st_src), .in1(splitter_1_al_src1), .out(multiplexer_3_out), .sel(not_2_out));
  Multiplexer #(.width(4), .enable("false")) multiplexer_4 (
    .in0(multiplexer_3_out), .in1(splitter_1_op1), .out(multiplexer_4_out), .sel(control_unit_1_br_en));
  _6to16sExtend _6to16sExtend (._6bitInput(splitter_1_immdata), ._16bitOuput(_6to16sExtend__16bitouput));
  _11to15zExtend _11to15zExtend (.in_1(splitter_1_ld_st_addr), .out_2(_11to15zExtend_out_2));
  Register_File register_file_1 (
    .SRC1(multiplexer_4_out), .SRC2(multiplexer_2_out), .InData(multiplexer_6_out),
    .DST(splitter_1_al_ld_dst), .WE(control_unit_1_regwrite), .Clock(clock_1_out),
    .OutData2(register_file_1_outdata2), .OutData1(register_file_1_outdata1));
  Multiplexer #(.width(16), .enable("false")) multiplexer_5 (
    .in0(_6to16sExtend__16bitouput), .in1(register_file_1_outdata2), .out(multiplexer_5_out), .sel(not_1_out));
  ALU_16bit alu_16bit_1 (
    .ALU_in2(multiplexer_5_out), .ALU_in1(register_file_1_outdata1), .Enable(control_unit_1_aluenable),
    .ALUControl(control_unit_1_alucontrol), .Carry_Out(carry_out), .ALU_out(alu_16bit_1_alu_out));
  Multiplexer #(.width(16), .enable("false")) multiplexer_6 (
    .in0(alu_16bit_1_alu_out), .in1(ram_1_data), .out(multiplexer_6_out), .sel(control_unit_1_datamemread));
  RAM #(.addrWidth(15), .dataWidth(16), .bus("separate")) ram_1 (
    .addr(_11to15zExtend_out_2), .din(register_file_1_outdata1), .data(ram_1_data),
    .str(control_unit_1_datamemwrite), .clk(clock_1_out), .ld(control_unit_1_datamemread));  // open: sel, clr

  // Notes on the sheet:
  //   jmp addr or br addr
  //   INSTRUCTION MEMORY
  //   contents of rom_1 (hex, n*v repeats v):
  //   1a9c 2b002 39781 2b803 3e10f 20002 7d 2384 2d811 8945 3c342 30802 191c8 3a261 31805 2d81b 27ff8 2ad9
  //   1259 3b201 aa18 1308c 1b988 3a98
  //   BR or AL
  //   ST or AL
  //   BR or others
  //   Imm or Reg
  //   DATA MEMORY
  //   AL or      LD
endmodule

// CONTROL UNIT
module Control_Unit (
  input  [2:0] Opcode,
  input  [2:0] nzp,
  input  Clock,
  output ALUEnable,
  output [1:0] ALUControl,
  output PC_1,
  output DataMemRead,
  output RegWrite,
  output DataMemWrite,
  output PCWrite,
  output BR_en,
  output [2:0] BRControl
);

  wire AL__LD2___ST_out, and_1_out, decoder_1_out0, decoder_1_out1, decoder_1_out2, decoder_1_out3,
       decoder_1_out4, decoder_1_out13, JMP_BR_out, or_1_out, PC_update_signal_of_previous_turn_q;
  wire [3:0] multiplexer_1_out, register_1_q;
  wire [3:2] controlled_buffer_1_out;

  Multiplexer #(.width(4), .enable("false")) multiplexer_1 (
    .in0({1'b0, Opcode}), .in1(4'b1101), .out(multiplexer_1_out), .sel(DataMemRead));
  Register #(.width(4)) register_1 (.D(multiplexer_1_out), .Q(register_1_q), .clk(Clock));  // open: en, clr
  Register #(.width(1)) PC_update_signal_of_previous_turn (
    .D(or_1_out), .Q(PC_update_signal_of_previous_turn_q), .clk(Clock));  // open: en, clr
  Decoder #(.select(4), .enable("false")) decoder_1 (
    .out0(decoder_1_out0), .out1(decoder_1_out1), .out2(decoder_1_out2), .out3(decoder_1_out3),
    .out4(decoder_1_out4), .out5(DataMemRead), .out6(DataMemWrite), .out7(BR_en), .out13(decoder_1_out13),
    .sel(register_1_q));  // open: out8, out9, out10, out11, out12, out14, out15
  and and_1 (and_1_out, PC_update_signal_of_previous_turn_q, DataMemRead);
  or AL_Inst (ALUEnable, decoder_1_out0, decoder_1_out1, decoder_1_out2, decoder_1_out3);
  assign {controlled_buffer_1_out, ALUControl} = ALUEnable ? register_1_q : 4'bz;  // Controlled_Buffer controlled_buffer_1
  or AL_LD2 (RegWrite, decoder_1_out13, decoder_1_out3, decoder_1_out2, decoder_1_out1, decoder_1_out0);
  or or_1 (or_1_out, AL__LD2___ST_out, JMP_BR_out);
  or JMP_BR (JMP_BR_out, decoder_1_out4, BR_en);
  or AL__LD2___ST (AL__LD2___ST_out, RegWrite, DataMemWrite);
  Multiplexer #(.enable("false")) multiplexer_2 (.in0(JMP_BR_out), .in1(1'b0), .out(PCWrite), .sel(and_1_out));
  Multiplexer #(.enable("false")) multiplexer_3 (.in0(AL__LD2___ST_out), .in1(1'b0), .out(PC_1), .sel(and_1_out));

  assign BRControl = nzp;

  // Notes on the sheet:
  //   if PC update signal of previous turn is 1 and current turn is LD; disable PC update signals
  //   0-3    AL
  //   4    JMP
  //   5    LD
  //   6    ST
  //   7    BR
  //   13    LD2
endmodule

// ALU
module ALU_16bit (
  input  [15:0] ALU_in2,
  input  [15:0] ALU_in1,
  input  Enable,
  input  [1:0] ALUControl,
  output Carry_Out,
  output [15:0] ALU_out
);

  wire [15:0] adder_16bit_1_sum, AND_out, OR_out, XOR_out;

  Adder_16bit adder_16bit_1 (.Carry_out(Carry_Out), .A(ALU_in1), .B(ALU_in2), .Sum(adder_16bit_1_sum));
  assign AND_out = ALU_in2 & ALU_in1;  // AND_Gate AND, 16 bits wide
  Multiplexer #(.select(2), .width(16)) multiplexer_1 (
    .in0(adder_16bit_1_sum), .in1(AND_out), .in2(OR_out), .in3(XOR_out), .out(ALU_out), .sel(ALUControl),
    .en(Enable));
  assign OR_out = ALU_in2 | ALU_in1;  // OR_Gate OR, 16 bits wide
  assign XOR_out = ALU_in2 ^ ALU_in1;  // XOR_Gate XOR, 16 bits wide
endmodule

module PC (
  input  [14:0] InputAddress,
  input  PCWrite,
  input  PC_1,
  input  Clock,
  output [14:0] OutputAddress
);

  wire or_1_out;
  wire [14:0] adder_1_out, multiplexer_1_out;

  Multiplexer #(.width(15), .enable("false")) multiplexer_1 (
    .in0(15'h1), .in1(InputAddress), .out(multiplexer_1_out), .sel(PCWrite));
  or or_1 (or_1_out, PCWrite, PC_1);
  Adder #(.width(15)) adder_1 (.a(multiplexer_1_out), .b(OutputAddress), .out(adder_1_out));  // open: cin, cout
  Register #(.width(15)) register_1 (.D(adder_1_out), .en(or_1_out), .Q(OutputAddress), .clk(Clock));  // open: clr
endmodule

module _6to16sExtend (
  input  [5:0] _6bitInput,
  output [15:0] _16bitOuput
);


  assign _16bitOuput = {{11{_6bitInput[5]}}, _6bitInput[4:0]};
endmodule

module _4to15zExtend (
  input  [3:0] in_1,
  output [14:0] out_2
);


  assign out_2 = {{11{1'b0}}, in_1};
endmodule

module _11to16zExtend (
  input  [10:0] _11bitInput,
  output [15:0] _15bitOutput
);


  assign _15bitOutput = {{5{1'b0}}, _11bitInput};
endmodule

module _11to15zExtend (
  input  [10:0] in_1,
  output [14:0] out_2
);


  assign out_2 = {4'b0000, in_1};
endmodule

// FA
module Full_Adder (
  input  A,
  input  B,
  input  Carry_in,
  output Sum,
  output Carry_out
);

  wire and_1_out, and_2_out, xor_1_out;

  xor xor_1 (xor_1_out, A, B);
  and and_1 (and_1_out, xor_1_out, Carry_in);
  and and_2 (and_2_out, A, B);
  or or_1 (Carry_out, and_1_out, and_2_out);
  xor xor_2 (Sum, xor_1_out, Carry_in);
endmodule

// HA
module Half_Adder (
  input  A,
  input  B,
  output Sum,
  output Carry_out
);

  and and_1 (Carry_out, A, B);
  xor xor_1 (Sum, A, B);
endmodule

// ADD
module Adder_16bit (
  input  [15:0] A,
  input  [15:0] B,
  output Carry_out,
  output [15:0] Sum
);

  wire full_adder_2_carry_out, full_adder_3_carry_out, full_adder_4_carry_out, full_adder_5_carry_out,
       full_adder_6_carry_out, full_adder_7_carry_out, full_adder_8_carry_out, full_adder_9_carry_out,
       full_adder_10_carry_out, full_adder_11_carry_out, full_adder_12_carry_out, full_adder_13_carry_out,
       full_adder_14_carry_out, full_adder_15_carry_out, half_adder_1_carry_out;

  Full_Adder full_adder_1 (
    .A(full_adder_2_carry_out), .B(B[15]), .Carry_in(A[15]), .Sum(Sum[15]), .Carry_out(Carry_out));
  Full_Adder full_adder_2 (
    .A(full_adder_3_carry_out), .B(B[14]), .Carry_in(A[14]), .Sum(Sum[14]), .Carry_out(full_adder_2_carry_out));
  Full_Adder full_adder_3 (
    .A(full_adder_4_carry_out), .B(B[13]), .Carry_in(A[13]), .Sum(Sum[13]), .Carry_out(full_adder_3_carry_out));
  Full_Adder full_adder_4 (
    .A(full_adder_5_carry_out), .B(B[12]), .Carry_in(A[12]), .Sum(Sum[12]), .Carry_out(full_adder_4_carry_out));
  Full_Adder full_adder_5 (
    .A(full_adder_7_carry_out), .B(B[11]), .Carry_in(A[11]), .Sum(Sum[11]), .Carry_out(full_adder_5_carry_out));
  Full_Adder full_adder_6 (
    .A(full_adder_8_carry_out), .B(B[9]), .Carry_in(A[9]), .Sum(Sum[9]), .Carry_out(full_adder_6_carry_out));
  Full_Adder full_adder_7 (
    .A(full_adder_6_carry_out), .B(B[10]), .Carry_in(A[10]), .Sum(Sum[10]), .Carry_out(full_adder_7_carry_out));
  Full_Adder full_adder_8 (
    .A(full_adder_9_carry_out), .B(B[8]), .Carry_in(A[8]), .Sum(Sum[8]), .Carry_out(full_adder_8_carry_out));
  Full_Adder full_adder_9 (
    .A(full_adder_10_carry_out), .B(B[7]), .Carry_in(A[7]), .Sum(Sum[7]), .Carry_out(full_adder_9_carry_out));
  Full_Adder full_adder_10 (
    .A(full_adder_11_carry_out), .B(B[6]), .Carry_in(A[6]), .Sum(Sum[6]), .Carry_out(full_adder_10_carry_out));
  Full_Adder full_adder_11 (
    .A(full_adder_12_carry_out), .B(B[5]), .Carry_in(A[5]), .Sum(Sum[5]), .Carry_out(full_adder_11_carry_out));
  Full_Adder full_adder_12 (
    .A(full_adder_13_carry_out), .B(B[4]), .Carry_in(A[4]), .Sum(Sum[4]), .Carry_out(full_adder_12_carry_out));
  Full_Adder full_adder_13 (
    .A(full_adder_14_carry_out), .B(B[3]), .Carry_in(A[3]), .Sum(Sum[3]), .Carry_out(full_adder_13_carry_out));
  Full_Adder full_adder_14 (
    .A(full_adder_15_carry_out), .B(B[2]), .Carry_in(A[2]), .Sum(Sum[2]), .Carry_out(full_adder_14_carry_out));
  Full_Adder full_adder_15 (
    .A(half_adder_1_carry_out), .B(B[1]), .Carry_in(A[1]), .Sum(Sum[1]), .Carry_out(full_adder_15_carry_out));
  Half_Adder half_adder_1 (.A(B[0]), .B(A[0]), .Sum(Sum[0]), .Carry_out(half_adder_1_carry_out));
endmodule

module Comparator_1bit (
  input  a,
  input  b,
  input  in_gt,
  input  in_eq,
  input  in_lt,
  output gt_out,
  output eq_out,
  output lt_out
);

  wire and_1_out, and_3_out, not_1_out, not_2_out, xnor_1_out;

  not not_1 (not_1_out, b);
  xnor xnor_1 (xnor_1_out, a, b);
  not not_2 (not_2_out, a);
  and and_1 (and_1_out, a, not_1_out, in_eq);
  and and_2 (eq_out, xnor_1_out, in_eq);
  and and_3 (and_3_out, not_2_out, b, in_eq);
  or or_1 (gt_out, in_gt, and_1_out);
  or or_2 (lt_out, in_lt, and_3_out);
endmodule

module Branch__Signed_Comparator_16bit (
  input  [15:0] A,
  input  BR_en,
  input  [15:0] B,
  input  [2:0] Branch_Control,
  output result_T_F
);

  wire and_1_out, and_2_out, comparator_1bit_1_eq_out, comparator_1bit_1_gt_out, comparator_1bit_1_lt_out,
       comparator_1bit_2_eq_out, comparator_1bit_2_gt_out, comparator_1bit_2_lt_out,
       comparator_1bit_3_eq_out, comparator_1bit_3_gt_out, comparator_1bit_3_lt_out,
       comparator_1bit_4_eq_out, comparator_1bit_4_gt_out, comparator_1bit_4_lt_out,
       comparator_1bit_5_eq_out, comparator_1bit_5_gt_out, comparator_1bit_5_lt_out,
       comparator_1bit_6_eq_out, comparator_1bit_6_gt_out, comparator_1bit_6_lt_out,
       comparator_1bit_7_eq_out, comparator_1bit_7_gt_out, comparator_1bit_7_lt_out,
       comparator_1bit_8_eq_out, comparator_1bit_8_gt_out, comparator_1bit_8_lt_out,
       comparator_1bit_9_eq_out, comparator_1bit_9_gt_out, comparator_1bit_9_lt_out,
       comparator_1bit_10_eq_out, comparator_1bit_10_gt_out, comparator_1bit_10_lt_out,
       comparator_1bit_11_eq_out, comparator_1bit_11_gt_out, comparator_1bit_11_lt_out,
       comparator_1bit_12_eq_out, comparator_1bit_12_gt_out, comparator_1bit_12_lt_out,
       comparator_1bit_13_eq_out, comparator_1bit_13_gt_out, comparator_1bit_13_lt_out,
       comparator_1bit_14_eq_out, comparator_1bit_14_gt_out, comparator_1bit_14_lt_out,
       comparator_1bit_15_eq_out, comparator_1bit_15_gt_out, comparator_1bit_15_lt_out,
       controlled_buffer_1_out, decoder_1_out1, decoder_1_out2, decoder_1_out3, decoder_1_out4,
       decoder_1_out6, or_1_out, or_2_out, xnor_1_out;

  xnor xnor_1 (xnor_1_out, A[15], B[15]);
  and and_1 (and_1_out, A[15], ~B[15]);  // AND_Gate
  and and_2 (and_2_out, ~A[15], B[15]);  // AND_Gate
  Comparator_1bit comparator_1bit_1 (
    .in_gt(and_2_out), .in_eq(xnor_1_out), .in_lt(and_1_out), .a(A[14]), .b(B[14]),
    .gt_out(comparator_1bit_1_gt_out), .eq_out(comparator_1bit_1_eq_out), .lt_out(comparator_1bit_1_lt_out));
  Comparator_1bit comparator_1bit_2 (
    .in_gt(comparator_1bit_3_gt_out), .in_eq(comparator_1bit_3_eq_out), .in_lt(comparator_1bit_3_lt_out),
    .a(A[12]), .b(B[12]), .gt_out(comparator_1bit_2_gt_out), .eq_out(comparator_1bit_2_eq_out),
    .lt_out(comparator_1bit_2_lt_out));
  Comparator_1bit comparator_1bit_3 (
    .in_gt(comparator_1bit_1_gt_out), .in_eq(comparator_1bit_1_eq_out), .in_lt(comparator_1bit_1_lt_out),
    .a(A[13]), .b(B[13]), .gt_out(comparator_1bit_3_gt_out), .eq_out(comparator_1bit_3_eq_out),
    .lt_out(comparator_1bit_3_lt_out));
  Comparator_1bit comparator_1bit_4 (
    .in_gt(comparator_1bit_2_gt_out), .in_eq(comparator_1bit_2_eq_out), .in_lt(comparator_1bit_2_lt_out),
    .a(A[11]), .b(B[11]), .gt_out(comparator_1bit_4_gt_out), .eq_out(comparator_1bit_4_eq_out),
    .lt_out(comparator_1bit_4_lt_out));
  Comparator_1bit comparator_1bit_5 (
    .in_gt(comparator_1bit_4_gt_out), .in_eq(comparator_1bit_4_eq_out), .in_lt(comparator_1bit_4_lt_out),
    .a(A[10]), .b(B[10]), .gt_out(comparator_1bit_5_gt_out), .eq_out(comparator_1bit_5_eq_out),
    .lt_out(comparator_1bit_5_lt_out));
  Comparator_1bit comparator_1bit_6 (
    .in_gt(comparator_1bit_5_gt_out), .in_eq(comparator_1bit_5_eq_out), .in_lt(comparator_1bit_5_lt_out),
    .a(A[9]), .b(B[9]), .gt_out(comparator_1bit_6_gt_out), .eq_out(comparator_1bit_6_eq_out),
    .lt_out(comparator_1bit_6_lt_out));
  Comparator_1bit comparator_1bit_7 (
    .in_gt(comparator_1bit_6_gt_out), .in_eq(comparator_1bit_6_eq_out), .in_lt(comparator_1bit_6_lt_out),
    .a(A[8]), .b(B[8]), .gt_out(comparator_1bit_7_gt_out), .eq_out(comparator_1bit_7_eq_out),
    .lt_out(comparator_1bit_7_lt_out));
  Comparator_1bit comparator_1bit_8 (
    .in_gt(comparator_1bit_7_gt_out), .in_eq(comparator_1bit_7_eq_out), .in_lt(comparator_1bit_7_lt_out),
    .a(A[7]), .b(B[7]), .gt_out(comparator_1bit_8_gt_out), .eq_out(comparator_1bit_8_eq_out),
    .lt_out(comparator_1bit_8_lt_out));
  Comparator_1bit comparator_1bit_9 (
    .in_gt(comparator_1bit_8_gt_out), .in_eq(comparator_1bit_8_eq_out), .in_lt(comparator_1bit_8_lt_out),
    .a(A[6]), .b(B[6]), .gt_out(comparator_1bit_9_gt_out), .eq_out(comparator_1bit_9_eq_out),
    .lt_out(comparator_1bit_9_lt_out));
  Comparator_1bit comparator_1bit_10 (
    .in_gt(comparator_1bit_9_gt_out), .in_eq(comparator_1bit_9_eq_out), .in_lt(comparator_1bit_9_lt_out),
    .a(A[5]), .b(B[5]), .gt_out(comparator_1bit_10_gt_out), .eq_out(comparator_1bit_10_eq_out),
    .lt_out(comparator_1bit_10_lt_out));
  Comparator_1bit comparator_1bit_11 (
    .in_gt(comparator_1bit_10_gt_out), .in_eq(comparator_1bit_10_eq_out), .in_lt(comparator_1bit_10_lt_out),
    .a(A[4]), .b(B[4]), .gt_out(comparator_1bit_11_gt_out), .eq_out(comparator_1bit_11_eq_out),
    .lt_out(comparator_1bit_11_lt_out));
  Comparator_1bit comparator_1bit_12 (
    .in_gt(comparator_1bit_11_gt_out), .in_eq(comparator_1bit_11_eq_out), .in_lt(comparator_1bit_11_lt_out),
    .a(A[3]), .b(B[3]), .gt_out(comparator_1bit_12_gt_out), .eq_out(comparator_1bit_12_eq_out),
    .lt_out(comparator_1bit_12_lt_out));
  Comparator_1bit comparator_1bit_13 (
    .in_gt(comparator_1bit_12_gt_out), .in_eq(comparator_1bit_12_eq_out), .in_lt(comparator_1bit_12_lt_out),
    .a(A[2]), .b(B[2]), .gt_out(comparator_1bit_13_gt_out), .eq_out(comparator_1bit_13_eq_out),
    .lt_out(comparator_1bit_13_lt_out));
  Comparator_1bit comparator_1bit_14 (
    .in_gt(comparator_1bit_13_gt_out), .in_eq(comparator_1bit_13_eq_out), .in_lt(comparator_1bit_13_lt_out),
    .a(A[1]), .b(B[1]), .gt_out(comparator_1bit_14_gt_out), .eq_out(comparator_1bit_14_eq_out),
    .lt_out(comparator_1bit_14_lt_out));
  Comparator_1bit comparator_1bit_15 (
    .in_gt(comparator_1bit_14_gt_out), .in_eq(comparator_1bit_14_eq_out), .in_lt(comparator_1bit_14_lt_out),
    .a(A[0]), .b(B[0]), .gt_out(comparator_1bit_15_gt_out), .eq_out(comparator_1bit_15_eq_out),
    .lt_out(comparator_1bit_15_lt_out));
  Decoder #(.select(3), .enable("false")) decoder_1 (
    .out1(decoder_1_out1), .out2(decoder_1_out2), .out3(decoder_1_out3), .out4(decoder_1_out4),
    .out6(decoder_1_out6), .sel(Branch_Control));  // open: out0, out5, out7
  or or_1 (or_1_out, comparator_1bit_15_lt_out, comparator_1bit_15_eq_out);
  or or_2 (or_2_out, comparator_1bit_15_gt_out, comparator_1bit_15_eq_out);
  assign controlled_buffer_1_out = decoder_1_out3 ? or_2_out : 1'bz;  // Controlled_Buffer controlled_buffer_1
  assign controlled_buffer_1_out = decoder_1_out6 ? or_1_out : 1'bz;  // Controlled_Buffer controlled_buffer_2
  assign controlled_buffer_1_out = decoder_1_out1 ? comparator_1bit_15_gt_out : 1'bz;  // Controlled_Buffer controlled_buffer_3
  assign controlled_buffer_1_out = decoder_1_out2 ? comparator_1bit_15_eq_out : 1'bz;  // Controlled_Buffer controlled_buffer_4
  assign controlled_buffer_1_out = decoder_1_out4 ? comparator_1bit_15_lt_out : 1'bz;  // Controlled_Buffer controlled_buffer_5
  Multiplexer #(.enable("false")) multiplexer_1 (
    .in0(1'b0), .in1(controlled_buffer_1_out), .out(result_T_F), .sel(BR_en));

  // Notes on the sheet:
  //   First bit signs:
  //   0-0
  //   1-1
  //   eq_in
  //   1-0
  //   gt_in
  //   lt_in
  //   0-1
  //   bgt
  //   beq
  //   bge
  //   blt
  //   ble
endmodule
